// Logisim project ejercicio_4.circ as structural Verilog: 2 circuits, main circuit main
module main (
);

  wire button_1_out;
  wire [2:0] dipswitch_1_sw1, shift_clase_1_s;

  DipSwitch #(.number(3)) dipswitch_1 (.sw1(dipswitch_1_sw1[0]), .sw2(dipswitch_1_sw1[1]), .sw3(dipswitch_1_sw1[2]));
  Button button_1 (.out(button_1_out));
  shift_clase shift_clase_1 (.E(dipswitch_1_sw1), .C(button_1_out), .S(shift_clase_1_s));
  LedBar #(.matrixcols(3)) ledbar_1 (.led0(shift_clase_1_s[0]), .led1(shift_clase_1_s[1]), .led2(shift_clase_1_s[2]));
endmodule

module shift_clase (
  input  [2:0] E,
  input  C,
  output [2:0] S
);

  wire and_1_out, and_4_out, not_1_out;

  not not_1 (not_1_out, C);
  and and_1 (and_1_out, E[0], C);
  and and_2 (S[0], E[1], not_1_out);
  and and_3 (S[2], C, E[1]);
  and and_4 (and_4_out, E[2], not_1_out);
  or or_1 (S[1], and_1_out, and_4_out);
endmodule
